# Fritzing sketch RS485_circuit (saved by Fritzing 0.9.9b)

parts:
  USBTTL1 = USB TTL Serial Cable
  Component1 = RS485_XY-017 [part_number=XY-017]
  M1 = DOIT Esp32 DevKit v1 (30 pins long, 11 pins width) [part_number=ESP32S-PIN30]

nets:
  N1: USBTTL1.TX, Component1.B
  N2: USBTTL1.5V, Component1.A
  GND: Component1.GND, M1.GND
  VCC: Component1.VCC, M1.3V3
  N3: Component1.TXD, M1.TX2
  N4: Component1.RXD, M1.RX2

notes:
  USB to RS485 module
  red -> A +, green -> B-
  white -> 5 V, Black -> GND
  RS485 XY-017

custom parts:
  RS485_XY-017: Commercially available RS485 to RS232 TTL Module
  DOIT Esp32 DevKit v1 (30 pins long, 11 pins width): The DOIT Esp32 DevKit v1 is one of the development board created by DOIT to evaluate the ESP-WROOM-32 module. It is based on the ESP32 microcontroller that boasts Wifi, Bluetooth, Ethernet and Low Power support all in a single chip. (vanepp) made breadboard work, adjusted pin numbering and labels and reduced size of schematic and cleaned up pcb. This chip is 30pins long (2 x15) and 11 pins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
